# Fritzing sketch Game Ping-Pong (saved by Fritzing 0.9.4)
breadboards: 1

parts:
  Componente1 = LED Matrix - Serial Interface - Red/Green/Blue
  Componente2 = LED Matrix - Serial Interface - Red/Green/Blue
  Componente3 = Arduino Pro Mini (3.3V)  # not connected
  U2 = POT [package=alps_pot]
  J1 = Piezo Speaker
  R1 = Resistor [tolerance=±5% resistance=220 package="0402 [SMD]"]
  Q1 = NPN-Transistor [package="TO92 [THT]"]
  U3 = SWITCH-SPST-2 [package=switch-spst-vertical]
  BAT1 = BC9VPC [package=bc9vpc]

nets:
  N1: Componente1.SCK, Componente2.SCK
  N2: Componente1.CS, Componente2.CS
  N3: Componente1.MISO, Componente2.MOSI
  GND: Componente1.GND, Componente2.GND, U2.A, J1.pin2
  N4: Componente1.MOSI, U2.E, Q1.E, BAT1.V-
  N5: J1.pin1, Q1.C
  N6: R1.Pin_1, Q1.B
  N7: U3.O, BAT1.V+

notes:
  NPN 2SC1815
  POT 10K
  Buzzer 5v
  Arduino Pro Mini
